# Fritzing sketch Circuit (saved by Fritzing 0.4.3b)
breadboards: 1

parts:
  Arduino1 = Arduino
  J1 = Piezo Speaker
  Part1 = Parallax Ping

nets:
  N1: Arduino1.D10, J1.pin2
  N2: Arduino1.D7, Part1.connector2
  N3: Arduino1.+5V, J1.pin1, Part1.connector1
  N4: Arduino1.GND, Part1.connector0
